# Fritzing sketch moduloIN_v2 (saved by Fritzing 1.0.2b)
circuit board: 11.2cm x 8.2cm
breadboards: 2

parts:
  U16 = Sharp PC817 [package=THT]
  U15 = Sharp PC817 [package=THT]
  U2 = Sharp PC817 [package=THT]
  U3 = Sharp PC817 [package=THT]
  U4 = Sharp PC817 [package=THT]
  U5 = Sharp PC817 [package=THT]
  U6 = Sharp PC817 [package=THT]
  U7 = Sharp PC817 [package=THT]
  U8 = Sharp PC817 [package=THT]
  U9 = Sharp PC817 [package=THT]
  U10 = Sharp PC817 [package=THT]
  U11 = Sharp PC817 [package=THT]
  U12 = Sharp PC817 [package=THT]
  U13 = Sharp PC817 [package=THT]
  U14 = Sharp PC817 [package=THT]
  U1 = Sharp PC817 [package=THT]
  R1 = Resistor [tolerance=±5% resistance=1k power=0.25W package=THT]
  R2 = Resistor [tolerance=±5% resistance=1k power=0.25W package=THT]
  R3 = Resistor [tolerance=±5% resistance=1k power=0.25W package=THT]
  R4 = Resistor [tolerance=±5% resistance=1k power=0.25W package=THT]
  R5 = Resistor [tolerance=±5% resistance=1k power=0.25W package=THT]
  R6 = Resistor [tolerance=±5% resistance=1k power=0.25W package=THT]
  R7 = Resistor [tolerance=±5% resistance=1k power=0.25W package=THT]
  R8 = Resistor [tolerance=±5% resistance=1k power=0.25W package=THT]
  R9 = Resistor [tolerance=±5% resistance=1k power=0.25W package=THT]
  R10 = Resistor [tolerance=±5% resistance=1k power=0.25W package=THT]
  R11 = Resistor [tolerance=±5% resistance=1k power=0.25W package=THT]
  R13 = Resistor [tolerance=±5% resistance=1k power=0.25W package=THT]
  R15 = Resistor [tolerance=±5% resistance=1k power=0.25W package=THT]
  R16 = Resistor [tolerance=±5% resistance=1k power=0.25W package=THT]
  R14 = Resistor [tolerance=±5% resistance=1k power=0.25W package=THT]
  J1 = Dagu DGServo 9g header (male) [package=THT]
  J2 = Dagu DGServo 9g header (male) [package=THT]
  J1_2 = Dagu DGServo 9g header (male) [package=THT]
  J2_2 = Dagu DGServo 9g header (male) [package=THT]
  R12 = Resistor [tolerance=±5% resistance=1k power=0.25W package=THT]
  A1 = Dagu DGServo 9g header (male) [package=THT]
  A0 = Dagu DGServo 9g header (male) [package=THT]
  R0 = Resistor [tolerance=±5% resistance=10k power=0.25W package=THT]
  MCP23017-E/SP = MCP23017 [package="DIP (Dual Inline) [THT]"]
  GND_IN1 = screw terminal, 2 pins
  IN2_IN3 = screw terminal, 2 pins
  IN4_GND = screw terminal, 2 pins
  IN5_IN6 = screw terminal, 2 pins
  IN7_IN8 = screw terminal, 2 pins
  IN9_GND = screw terminal, 2 pins
  IN11_IN10 = screw terminal, 2 pins
  GND_IN12 = screw terminal, 2 pins
  IN14_IN13 = screw terminal, 2 pins
  IN16_IN15 = screw terminal, 2 pins

nets:
  N1: U16.Pin_1, R16.Pin_1
  N2: U16.Pin_2, IN16_IN15.pin2
  N3: U16.Pin_4, MCP23017-E/SP.GPB0
  GND: U16.Pin_3, U15.Pin_3, U2.Pin_3, U3.Pin_3, U4.Pin_3, U5.Pin_3, U6.Pin_3, U7.Pin_3, U8.Pin_3, U9.Pin_3, U10.Pin_3, U11.Pin_3, U12.Pin_3, U13.Pin_3, U14.Pin_3, U1.Pin_3, J1.gnd, J1_2.gnd, A1.gnd, A0.gnd, MCP23017-E/SP.GND, MCP23017-E/SP.A2, GND_IN1.pin1, IN4_GND.pin2, IN9_GND.pin1, GND_IN12.pin2
  N4: U15.Pin_1, R15.Pin_1
  N5: U15.Pin_2, IN16_IN15.pin1
  N6: U15.Pin_4, MCP23017-E/SP.GPB1
  N7: U2.Pin_1, R2.Pin_1
  N8: U2.Pin_2, IN2_IN3.pin1
  N9: U2.Pin_4, MCP23017-E/SP.GPA6
  N10: U3.Pin_1, R3.Pin_1
  N11: U3.Pin_2, IN2_IN3.pin2
  N12: U3.Pin_4, MCP23017-E/SP.GPA5
  N13: U4.Pin_1, R4.Pin_1
  N14: U4.Pin_2, IN4_GND.pin1
  N15: U4.Pin_4, MCP23017-E/SP.GPA4
  N16: U5.Pin_1, R5.Pin_1
  N17: U5.Pin_2, IN5_IN6.pin1
  N18: U5.Pin_4, MCP23017-E/SP.GPA3
  N19: U6.Pin_1, R6.Pin_1
  N20: U6.Pin_2, IN5_IN6.pin2
  N21: U6.Pin_4, MCP23017-E/SP.GPA2
  N22: U7.Pin_1, R7.Pin_1
  N23: U7.Pin_2, IN7_IN8.pin1
  N24: U7.Pin_4, MCP23017-E/SP.GPA1
  N25: U8.Pin_1, R8.Pin_1
  N26: U8.Pin_2, IN7_IN8.pin2
  N27: U8.Pin_4, MCP23017-E/SP.GPA0
  N28: U9.Pin_1, R9.Pin_1
  N29: U9.Pin_2, IN9_GND.pin2
  N30: U9.Pin_4, MCP23017-E/SP.GPB7
  N31: U10.Pin_1, R10.Pin_1
  N32: U10.Pin_2, IN11_IN10.pin1
  N33: U10.Pin_4, MCP23017-E/SP.GPB6
  N34: U11.Pin_1, R11.Pin_1
  N35: U11.Pin_2, IN11_IN10.pin2
  N36: U11.Pin_4, MCP23017-E/SP.GPB5
  N37: U12.Pin_1, R12.Pin_1
  N38: U12.Pin_2, GND_IN12.pin1
  N39: U12.Pin_4, MCP23017-E/SP.GPB4
  N40: U13.Pin_1, R13.Pin_1
  N41: U13.Pin_2, IN14_IN13.pin1
  N42: U13.Pin_4, MCP23017-E/SP.GPB3
  N43: U14.Pin_1, R14.Pin_1
  N44: U14.Pin_2, IN14_IN13.pin2
  N45: U14.Pin_4, MCP23017-E/SP.GPB2
  N46: U1.Pin_1, R1.Pin_1
  N47: U1.Pin_2, GND_IN1.pin2
  N48: U1.Pin_4, MCP23017-E/SP.GPA7
  VCC: R1.Pin_0, R2.Pin_0, R3.Pin_0, R4.Pin_0, R5.Pin_0, R6.Pin_0, R7.Pin_0, R8.Pin_0, R9.Pin_0, R10.Pin_0, R11.Pin_0, R13.Pin_0, R15.Pin_0, R16.Pin_0, R14.Pin_0, J1.Vcc, J1_2.Vcc, R12.Pin_0
  N49: J1.pulse, J1_2.pulse, A1.pulse, A0.pulse, MCP23017-E/SP.VCC
  GND_2: J2.gnd, J2_2.gnd, MCP23017-E/SP.SCL
  VCC_2: J2.Vcc, J2_2.Vcc, R0.Pin_1
  N50: J2.pulse, J2_2.pulse, MCP23017-E/SP.SDA
  N51: A1.Vcc, MCP23017-E/SP.A1
  N52: A0.Vcc, MCP23017-E/SP.A0
  N53: R0.Pin_0, MCP23017-E/SP.RST

notes:
  SDA
  RST
  SCL
  GND
  5V
  12V

custom parts:
  MCP23017: 16 bit I/O chip controlled via I2C
