# Fritzing sketch modulo_mcu_v2 (saved by Fritzing 1.0.2b)
circuit board: 11.2cm x 8.2cm
breadboards: 2

parts:
  J2 = Dagu DGServo 9g header (male) [package=THT]
  J1 = Dagu DGServo 9g header (male) [package=THT]
  C1 = Capacitor Polarized [part_number="10uF 10V" package=cpol-radial-10uf-25v]
  Lan_W5100 = W5100 mini [package=W5100]
  Arduino_Nano = Arduino Nano (Rev3.0)
  Q1 = NPN-Transistor [part_number=BC337 package="TO92 [THT]"]
  R3 = Resistor [tolerance=±5% resistance=4.7k power=0.25W package=THT]
  R4 = Resistor [tolerance=±5% resistance=2.2k power=0.25W package=THT]
  R2 = Resistor [tolerance=±5% resistance=4.7k power=0.25W package=THT]
  C2 = Electrolytic Capacitor [capacitance=1µF voltage=10V package="100 mil [THT, electrolytic]"]
  R1 = Resistor [tolerance=±5% resistance=220 power=1W package=THT]
  D3 = Rectifier Diode 10A [part_number=P1000K]
  D1 = Rectifier Diode 10A [part_number=P1000K]
  D2 = Rectifier Diode 10A [part_number=P1000K]
  Step_Down_5V = DC-DC Step Down [chip_label=LM2596S package=breakout]
  GND_BAT+ = screw terminal, 2 pins
  GND_12V+ = screw terminal, 2 pins
  ALARM_BAT = screw terminal, 2 pins

nets:
  N1: J2.gnd, Arduino_Nano.A5
  N2: J2.Vcc, Lan_W5100.RESET, Arduino_Nano.D4
  N3: J2.pulse, Arduino_Nano.A4
  GND: J1.gnd, C1.-, Lan_W5100.GND, Arduino_Nano.GND, Q1.E, R4.Pin_1, C2.-, Step_Down_5V.IN-, Step_Down_5V.OUT-, GND_BAT+.pin2, GND_12V+.pin2
  N4: J1.Vcc, R3.Pin_0, D1.cathode, D2.cathode, Step_Down_5V.IN+
  VCC: J1.pulse, Lan_W5100.VCC, Arduino_Nano.5V, Step_Down_5V.OUT+
  N5: C1.+, Arduino_Nano.RESET, Arduino_Nano.D5
  N6: Lan_W5100.MOSI, Arduino_Nano.D11/MOSI
  N7: Lan_W5100.MISO, Arduino_Nano.D12/MISO
  N8: Lan_W5100.SCK, Arduino_Nano.D13/SCK
  N9: Lan_W5100.SS, Arduino_Nano.D10
  N10: Q1.B, R4.Pin_0, R2.Pin_1, C2.+
  N11: Q1.C, R3.Pin_1, ALARM_BAT.pin1, ALARM_BAT.pin2
  N12: R2.Pin_0, D3.anode, GND_12V+.pin1
  N13: R1.Pin_0, D3.cathode, D2.anode
  N14: R1.Pin_1, D1.anode, GND_BAT+.pin1

notes:
  SDA
  12V
  5V
  GND
  SCL
  RST

custom parts:
  W5100 mini: WIZnet W5100 Network Module Mini
  Rectifier Diode 10A: A standard rectifier diode 10A
  DC-DC Step Down: DC-DC Step Down based on LM2596S
