# Fritzing sketch raspberry mcu (saved by Fritzing 0.9.4)
circuit board: 11.2cm x 8.2cm
breadboards: 2

parts:
  J2 = Dagu DGServo 9g header (male) [package=THT]
  J1 = Dagu DGServo 9g header (male) [package=THT]
  R3 = Resistor [tolerance=±5% resistance=4.7k package=THT]
  R4 = Resistor [tolerance=±5% resistance=2.2k package=THT]
  R2 = Resistor [tolerance=±5% resistance=4.7k package=THT]
  C2 = Electrolytic Capacitor [capacitance=1µF voltage=10V package="100 mil [THT, electrolytic]"]
  ALARM_BAT = screw terminal, 2 pins
  GND_BAT+ = screw terminal, 2 pins
  R1 = Resistor [tolerance=±5% resistance=220 power=1W package=THT]
  GND_12V+ = screw terminal, 2 pins
  D3 = Rectifier Diode 10A [part_number=P1000K]
  D1 = Rectifier Diode 10A [part_number=P1000K]
  D2 = Rectifier Diode 10A [part_number=P1000K]
  Step_Down_5V = DC-DC Step Down [chip_label=LM2596S package=breakout]
  Q1 = NPN-Transistor [part_number=BC337 package="TO92 [THT]"]
  Raspberry_Pi_1 = Raspberry Pi 3 [part_number=RPI-3-V1.2]

nets:
  N1: J2.gnd, Raspberry_Pi_1.GPIO3
  N2: J2.pulse, Raspberry_Pi_1.GPIO2
  GND: J1.gnd, R4.Pin_1, C2.-, GND_BAT+.pin2, GND_12V+.pin2, Step_Down_5V.IN-, Step_Down_5V.OUT-, Q1.E, Raspberry_Pi_1.GND
  N3: J1.Vcc, R3.Pin_0, R2.Pin_0, GND_12V+.pin1, D3.anode, D1.cathode, D2.cathode, Step_Down_5V.IN+
  N4: J1.pulse, Step_Down_5V.OUT+, Raspberry_Pi_1.5V
  N5: R3.Pin_1, ALARM_BAT.pin1, ALARM_BAT.pin2, Q1.C
  N6: R4.Pin_0, R2.Pin_1, C2.+, Q1.B
  N7: GND_BAT+.pin1, R1.Pin_1, D1.anode
  N8: R1.Pin_0, D3.cathode, D2.anode

custom parts:
  Rectifier Diode 10A: A standard rectifier diode 10A
  DC-DC Step Down: DC-DC Step Down based on LM2596S
